// Logisim project My-PC.circ as structural Verilog
module and_or_latch (
  input  set,
  input  reset,
  output \output 
);

  wire not_1_out, or_1_out;

  or or_1 (or_1_out, \output , set);
  not not_1 (not_1_out, reset);
  and and_1 (\output , or_1_out, not_1_out);
endmodule

module gated_latch (
  input  data_input,
  input  write_enable,
  output data_output
);

  wire and_1_out, and_2_out, not_1_out;

  not not_1 (not_1_out, data_input);
  and and_1 (and_1_out, data_input, write_enable);
  and_or_latch and_or_latch_1 (.set(and_1_out), .reset(and_2_out), .\output (data_output));
  and and_2 (and_2_out, not_1_out, write_enable);
endmodule

module latch_cell (
  input  write_enable,
  input  data_in,
  input  row,
  input  column,
  input  read_enable,
  output data_out
);

  wire and_1_out, and_2_out, and_3_out, gated_latch_1_data_output;

  and and_1 (and_1_out, row, column);
  gated_latch gated_latch_1 (.data_input(data_in), .write_enable(and_2_out), .data_output(gated_latch_1_data_output));
  and and_2 (and_2_out, write_enable, and_1_out);
  and and_3 (and_3_out, and_1_out, read_enable);
  and and_4 (data_out, gated_latch_1_data_output, and_3_out);
endmodule

module latch_row (
  input  data_in,
  input  write_enable,
  input  row,
  input  read_enable,
  input  column_0,
  input  column_1,
  input  column_2,
  input  column_3,
  input  column_4,
  input  column_5,
  input  column_6,
  input  column_7,
  output data_out
);

  wire latch_cell_1_data_out, latch_cell_2_data_out, latch_cell_3_data_out, latch_cell_4_data_out,
       latch_cell_5_data_out, latch_cell_6_data_out, latch_cell_7_data_out, latch_cell_8_data_out;

  latch_cell latch_cell_1 (
    .row(row), .write_enable(write_enable), .data_in(data_in), .column(column_0), .read_enable(read_enable),
    .data_out(latch_cell_1_data_out));
  latch_cell latch_cell_2 (
    .row(row), .write_enable(write_enable), .data_in(data_in), .column(column_1), .read_enable(read_enable),
    .data_out(latch_cell_2_data_out));
  latch_cell latch_cell_3 (
    .row(row), .write_enable(write_enable), .data_in(data_in), .column(column_2), .read_enable(read_enable),
    .data_out(latch_cell_3_data_out));
  latch_cell latch_cell_4 (
    .row(row), .write_enable(write_enable), .data_in(data_in), .column(column_3), .read_enable(read_enable),
    .data_out(latch_cell_4_data_out));
  latch_cell latch_cell_5 (
    .row(row), .write_enable(write_enable), .data_in(data_in), .column(column_4), .read_enable(read_enable),
    .data_out(latch_cell_5_data_out));
  or or_1 (data_out, latch_cell_1_data_out, latch_cell_2_data_out, latch_cell_3_data_out, latch_cell_4_data_out, latch_cell_5_data_out, latch_cell_6_data_out, latch_cell_7_data_out, latch_cell_8_data_out);
  latch_cell latch_cell_6 (
    .row(row), .write_enable(write_enable), .data_in(data_in), .column(column_5), .read_enable(read_enable),
    .data_out(latch_cell_6_data_out));
  latch_cell latch_cell_7 (
    .row(row), .write_enable(write_enable), .data_in(data_in), .column(column_6), .read_enable(read_enable),
    .data_out(latch_cell_7_data_out));
  latch_cell latch_cell_8 (
    .row(row), .write_enable(write_enable), .data_in(data_in), .column(column_7), .read_enable(read_enable),
    .data_out(latch_cell_8_data_out));
endmodule

module big_latch_row (
  input  column_8,
  input  column_9,
  input  read_enable,
  input  column_10,
  input  write_enable,
  input  column_11,
  input  column_12,
  input  column_13,
  input  column_14,
  input  column_0,
  input  column_15,
  input  column_1,
  input  column_2,
  input  data_in,
  input  column_3,
  input  row,
  input  column_4,
  input  column_5,
  input  column_6,
  input  column_7,
  output data_out
);

  wire latch_row_1_data_out, latch_row_2_data_out;

  latch_row latch_row_1 (
    .column_0(column_0), .column_1(column_1), .column_2(column_2), .column_3(column_3), .column_4(column_4),
    .column_5(column_5), .column_6(column_6), .column_7(column_7), .data_in(data_in),
    .write_enable(write_enable), .row(row), .read_enable(read_enable), .data_out(latch_row_1_data_out));
  or or_1 (data_out, latch_row_1_data_out, latch_row_2_data_out);
  latch_row latch_row_2 (
    .column_0(column_15), .column_1(column_14), .column_2(column_13), .column_3(column_12),
    .column_4(column_11), .column_5(column_10), .column_6(column_9), .column_7(column_8), .data_in(data_in),
    .write_enable(write_enable), .row(row), .read_enable(read_enable), .data_out(latch_row_2_data_out));
endmodule

module latch_matrix_4x16 (
  input  read_enable,
  input  data_in,
  input  row_0,
  input  row_1,
  input  write_enable,
  input  row_2,
  input  row_3,
  input  column_0,
  input  column_1,
  input  column_2,
  input  column_3,
  input  column_4,
  input  column_5,
  input  column_6,
  input  column_7,
  input  column_8,
  input  column_9,
  input  column_10,
  input  column_11,
  input  column_12,
  input  column_13,
  input  column_14,
  input  column_15,
  output data_out
);

  wire big_latch_row_1_data_out, big_latch_row_2_data_out, big_latch_row_3_data_out, big_latch_row_4_data_out;

  big_latch_row big_latch_row_1 (
    .column_0(column_0), .column_1(column_1), .column_2(column_2), .column_3(column_3), .column_4(column_4),
    .column_5(column_5), .column_6(column_6), .column_7(column_7), .read_enable(read_enable),
    .write_enable(write_enable), .row(row_0), .data_in(data_in), .column_8(column_8), .column_9(column_9),
    .column_10(column_10), .column_11(column_11), .data_out(big_latch_row_1_data_out), .column_12(column_12),
    .column_13(column_13), .column_14(column_14), .column_15(column_15));
  big_latch_row big_latch_row_2 (
    .column_0(column_0), .column_1(column_1), .column_2(column_2), .column_3(column_3), .column_4(column_4),
    .column_5(column_5), .column_6(column_6), .column_7(column_7), .read_enable(read_enable),
    .write_enable(write_enable), .row(row_1), .data_in(data_in), .column_8(column_8), .column_9(column_9),
    .column_10(column_10), .column_11(column_11), .data_out(big_latch_row_2_data_out), .column_12(column_12),
    .column_13(column_13), .column_14(column_14), .column_15(column_15));
  big_latch_row big_latch_row_3 (
    .column_0(column_0), .column_1(column_1), .column_2(column_2), .column_3(column_3), .column_4(column_4),
    .column_5(column_5), .column_6(column_6), .column_7(column_7), .read_enable(read_enable),
    .write_enable(write_enable), .row(row_2), .data_in(data_in), .column_8(column_8), .column_9(column_9),
    .column_10(column_10), .column_11(column_11), .data_out(big_latch_row_3_data_out), .column_12(column_12),
    .column_13(column_13), .column_14(column_14), .column_15(column_15));
  big_latch_row big_latch_row_4 (
    .column_0(column_0), .column_1(column_1), .column_2(column_2), .column_3(column_3), .column_4(column_4),
    .column_5(column_5), .column_6(column_6), .column_7(column_7), .read_enable(read_enable),
    .write_enable(write_enable), .row(row_3), .data_in(data_in), .column_8(column_8), .column_9(column_9),
    .column_10(column_10), .column_11(column_11), .data_out(big_latch_row_4_data_out), .column_12(column_12),
    .column_13(column_13), .column_14(column_14), .column_15(column_15));
  or or_1 (data_out, big_latch_row_1_data_out, big_latch_row_2_data_out, big_latch_row_3_data_out, big_latch_row_4_data_out);
endmodule

module latch_matrix_8x16 (
  input  row_0,
  input  row_1,
  input  row_2,
  input  row_3,
  input  row_4,
  input  row_5,
  input  row_6,
  input  row_7,
  input  read_enable,
  input  write_enable,
  input  data_in,
  input  column_0,
  input  column_1,
  input  column_2,
  input  column_3,
  input  column_4,
  input  column_5,
  input  column_6,
  input  column_7,
  input  column_8,
  input  column_9,
  input  column_10,
  input  column_11,
  input  column_12,
  input  column_13,
  input  column_14,
  input  column_15,
  output data_out
);

  wire latch_matrix_4x16_1_data_out, latch_matrix_4x16_2_data_out;

  latch_matrix_4x16 latch_matrix_4x16_1 (
    .read_enable(read_enable), .row_0(row_0), .row_1(row_1), .row_2(row_2), .row_3(row_3),
    .column_0(column_0), .column_1(column_1), .column_2(column_2), .column_3(column_3), .column_4(column_4),
    .column_5(column_5), .column_6(column_6), .column_7(column_7), .column_8(column_8), .column_9(column_9),
    .column_10(column_10), .column_11(column_11), .column_12(column_12), .column_13(column_13),
    .column_14(column_14), .column_15(column_15), .data_in(data_in), .data_out(latch_matrix_4x16_1_data_out),
    .write_enable(write_enable));
  latch_matrix_4x16 latch_matrix_4x16_2 (
    .read_enable(read_enable), .row_0(row_4), .row_1(row_5), .row_2(row_6), .row_3(row_7),
    .column_0(column_0), .column_1(column_1), .column_2(column_2), .column_3(column_3), .column_4(column_4),
    .column_5(column_5), .column_6(column_6), .column_7(column_7), .column_8(column_8), .column_9(column_9),
    .column_10(column_10), .column_11(column_11), .column_12(column_12), .column_13(column_13),
    .column_14(column_14), .column_15(column_15), .data_in(data_in), .data_out(latch_matrix_4x16_2_data_out),
    .write_enable(write_enable));
  or or_1 (data_out, latch_matrix_4x16_1_data_out, latch_matrix_4x16_2_data_out);
endmodule

module latch_matrix_16x16 (
  input  row_0,
  input  row_1,
  input  row_2,
  input  row_3,
  input  row_4,
  input  row_5,
  input  row_6,
  input  row_7,
  input  row_8,
  input  row_9,
  input  data_in,
  input  row_10,
  input  write_enable,
  input  row_11,
  input  read_enable,
  input  row_12,
  input  row_13,
  input  row_14,
  input  row_15,
  input  column_0,
  input  column_1,
  input  column_2,
  input  column_3,
  input  column_4,
  input  column_5,
  input  column_6,
  input  column_7,
  input  column_8,
  input  column_9,
  input  column_10,
  input  column_11,
  input  column_12,
  input  column_13,
  input  column_14,
  input  column_15,
  output data_out
);

  wire latch_matrix_8x16_1_data_out, latch_matrix_8x16_2_data_out;

  or or_1 (data_out, latch_matrix_8x16_2_data_out, latch_matrix_8x16_1_data_out);
  latch_matrix_8x16 latch_matrix_8x16_1 (
    .column_0(column_0), .column_1(column_1), .column_2(column_2), .column_3(column_3), .column_4(column_4),
    .column_5(column_5), .column_6(column_6), .column_7(column_7), .column_8(column_8), .column_9(column_9),
    .column_10(column_10), .column_11(column_11), .column_12(column_12), .column_13(column_13),
    .column_14(column_14), .column_15(column_15), .row_0(row_0), .row_1(row_1), .row_2(row_2), .row_3(row_3),
    .row_4(row_4), .row_5(row_5), .row_6(row_6), .row_7(row_7), .data_out(latch_matrix_8x16_1_data_out),
    .read_enable(read_enable), .write_enable(write_enable), .data_in(data_in));
  latch_matrix_8x16 latch_matrix_8x16_2 (
    .column_0(column_0), .column_1(column_1), .column_2(column_2), .column_3(column_3), .column_4(column_4),
    .column_5(column_5), .column_6(column_6), .column_7(column_7), .column_8(column_8), .column_9(column_9),
    .column_10(column_10), .column_11(column_11), .column_12(column_12), .column_13(column_13),
    .column_14(column_14), .column_15(column_15), .row_0(row_8), .row_1(row_9), .row_2(row_10),
    .row_3(row_11), .row_4(row_12), .row_5(row_13), .row_6(row_14), .row_7(row_15),
    .data_out(latch_matrix_8x16_2_data_out), .read_enable(read_enable), .write_enable(write_enable),
    .data_in(data_in));
endmodule

module ram_block (
);

  latch_matrix_16x16 latch_matrix_16x16_1 ();  // open: data_in, write_enable, read_enable, data_out, column_0, column_1, column_2, column_3, column_4, column_5, column_6, column_7, column_8, column_9, column_10, column_11, column_12, column_13, column_14, column_15, row_0, row_1, row_2, row_3, row_4, row_5, row_6, row_7, row_8, row_9, row_10, row_11, row_12, row_13, row_14, row_15
endmodule

module selector (
  input  in_1,
  input  in_2,
  input  in_3,
  input  in_4,
  output s0,
  output s1,
  output s2,
  output s3,
  output s4,
  output s5,
  output s6,
  output s7,
  output s8,
  output s9,
  output s10,
  output s11,
  output s12,
  output s13,
  output s14,
  output s15
);

  // NOT_Gate not_1 has open pins: in=in_1, out=open
  // NOT_Gate not_2 has open pins: in=in_2, out=open
  // NOT_Gate not_3 has open pins: in=in_3, out=open
  // NOT_Gate not_4 has open pins: in=in_4, out=open
endmodule
